// Digital circuit Processor.dig as structural Verilog
// Simple processor based on the MIPS architecture. 
// It is a Harvard single-cycle CPU.
// {{de Einfacher Prozessor, der an die MIPS-Architektur 
// angelehnt ist. Es handelt sich um eine Harvard 
// Single-Cycle CPU.}}
module Processor (
  input  Clock
);

  wire abs, ALU2D, alu_1_carry, alu_1_neg, alu_1_zero, branch_1_jmp, flags_1_co, flags_1_no, flags_1_zo, imm,
       ioR, ioW, ld, muxA, sf, src2D, st, stPC, WE;
  wire [2:0] br, muxB;
  wire [4:0] ALUop;
  wire [15:0] alu_1_y, driver_1_out, imreg_1_imm, multiplexer_1_out, multiplexer_2_out, pc_1_next, pc_1_pc,
       register_1_rdest, register_1_rsrc, rom_1_d, signext_1__5d, signext_1__5s, signext_1__9sd;

  ROM #(.AddrBits(16), .isProgramMemory("true"), .Bits(16), .Addr_Bits(16)) rom_1 (
    .A(pc_1_pc), .sel(1'b1), .D(rom_1_d));
  PC pc_1 (.ALU(alu_1_y), .C(Clock), .abs(abs), .rel(branch_1_jmp), .Next(pc_1_next), .PC(pc_1_pc));
  assign driver_1_out = stPC ? pc_1_next : 16'bz;  // Driver driver_1
  Control control_1 (
    .Op(rom_1_d[15:9]), .stPC(stPC), .WE(WE), .imm(imm), .absJmp(abs), .muxB(muxB), .srcToD(src2D),
    .muxA(muxA), .ALUToBus(ALU2D), .ALUop(ALUop), .storeFlags(sf), .Branch(br), .st(st), .ld(ld), .ioW(ioW),
    .ioR(ioR));
  Register register_1 (
    .WD(driver_1_out), .C(Clock), .src(rom_1_d[3:0]), .dest(rom_1_d[7:4]), .WE(WE), .Rdest(register_1_rdest),
    .Rsrc(register_1_rsrc));
  ImReg imreg_1 (.inst(rom_1_d), .en(imm), .C(Clock), .imm(imreg_1_imm));
  SignExt signext_1 (.inst(rom_1_d), ._5S(signext_1__5s), ._9SD(signext_1__9sd), ._5D(signext_1__5d));
  assign driver_1_out = src2D ? register_1_rsrc : 16'bz;  // Driver driver_2
  Multiplexer #(.Bits(16)) multiplexer_1 (
    .sel(muxA), .in_0(register_1_rdest), .in_1(register_1_rsrc), .out(multiplexer_1_out));
  Multiplexer #(.Selector_Bits(3), .Bits(16)) multiplexer_2 (
    .sel(muxB), .in_0(register_1_rsrc), .in_1(imreg_1_imm), .in_2({16{1'b0}}), .in_3({16{1'b0}}),
    .in_4({16{1'b0}}), .in_5(signext_1__5s), .in_6(signext_1__9sd), .in_7(signext_1__5d),
    .out(multiplexer_2_out));
  Branch branch_1 (.Z(flags_1_zo), .N(flags_1_no), .C(flags_1_co), .ctrl(br), .jmp(branch_1_jmp));
  ALU alu_1 (
    .A(multiplexer_1_out), .B(multiplexer_2_out), .Op(ALUop), .Y(alu_1_y), .Zero(alu_1_zero),
    .Neg(alu_1_neg), .Carry(alu_1_carry), .Ci(flags_1_co));
  assign driver_1_out = ALU2D ? alu_1_y : 16'bz;  // Driver driver_3
  Flags flags_1 (
    .Zi(alu_1_zero), .Ni(alu_1_neg), .Ci(alu_1_carry), .C(Clock), .store(sf), .Zo(flags_1_zo),
    .No(flags_1_no), .Co(flags_1_co));
  RAMSinglePort #(.AddrBits(16), .Bits(16), .Addr_Bits(16)) ramsingleport_1 (
    .A(alu_1_y), .str(st), .C(Clock), .ld(ld), .D(driver_1_out));
  Graphics graphics_1 (.A(alu_1_y), .R(ioR), .C(Clock), .W(ioW), .D(driver_1_out));

  // Other names for the same wires on the sheet: C = Clock

  // Notes on the sheet:
  //   Clock: Hz: 2147483647
  //   contents of rom_1 (hex, n*v repeats v):
  //   8000,1360,8190,1350,1490,1483,1425,143a,20e1,14fc,4cef,6e55,1821,3c2f,65f9,6e1e,205,
  //   216,1430,1420,14a0,8033,68c0,7a80,3c80,5e05,3c72,5e05,3c73,5e03,6e03,3c73,6401,14a3,
  //   741a,1801,1811,1821,3d24,65ec,1831,3d34,65e8,3091,ffff,7009,246,265,254,7c00,6fdd,
  //   1470,2031,2104,8058,68b0,1821,1801,8058,68b0,1831,1904,8058,68b0,1831,1904,8058,68b0,
  //   2021,2001,8058,68b0,2021,2001,8058,68b0,2031,2104,8058,68b0,2031,2104,8058,68b0,1821,
  //   1831,1905,6a0c,3d24,6206,3d34,6204,7a80,3c80,5e01,1871,6a0b,243,3744,442,446,7448,
  //   4efe,18e1,6a0f
endmodule
